# Fritzing sketch CO2Ampel_Schaltplan (saved by Fritzing 0.9.4)
breadboards: 1

parts:
  Mod1 = Heltec WiFi Kit 32 [part_number=HTIT-WB32LA]
  R1 = Resistor [tolerance=±1% resistance=47 package="2010 [SMD]"]
  R2 = Resistor [tolerance=±1% resistance=47 package="2010 [SMD]"]
  R3 = Resistor [tolerance=±1% resistance=47 package="2010 [SMD]"]
  LED1 = LED - 5mm [color="Red (633nm)" package="5 mm [THT]"]
  LED2 = LED - 5mm [color="Yellow (595nm)" package="5 mm [THT]"]
  LED3 = LED - 5mm [color="Green (560nm)" package="5 mm [THT]"]
  AM1 = AM2302 Humidity and Temperature Sensor
  TD-er1 = MH-Z19 CO2 sensor [part_number=MH-Z19]

nets:
  N1: Mod1.pin_2, TD-er1.TX
  N2: Mod1.pin_3, LED3.anode
  N3: Mod1.pin_4, TD-er1.RX
  N4: Mod1.pin_5, LED2.anode
  N5: Mod1.pin_6, AM1.DATA
  N6: Mod1.pin_7, LED1.anode
  GND: Mod1.pin_15, Mod1.pin_18, Mod1.pin_19, R1.Pin_1, R2.Pin_1, R3.Pin_1, AM1.GND, TD-er1.GND
  N7: Mod1.pin_16, Mod1.pin_21
  VDD: Mod1.pin_17, Mod1.pin_20, AM1.VDD, TD-er1.Vin
  N8: R1.Pin_0, LED1.cathode
  N9: R2.Pin_0, LED2.cathode
  N10: R3.Pin_0, LED3.cathode

custom parts:
  Heltec WiFi Kit 32: Heltec WiFi Kit 32 WiFi Kit 32 is a classic IoT dev-board designed & produced by Heltec Automation(TM). It’s a highly integrated product based on ESP32 + SX127x, it has Wi-Fi, BLE, LoRa functions, also Li-Po battery management system, 0.96″ OLED are also included. It’s the best choice for smart cities, smart farms, smart home, and IoT makers.
